// Logisim project Practica_Display.circ as structural Verilog: 1 circuit, main circuit main
module main (
);

  wire clock_1_out;
  wire [13:0] counter_1_q;
  wire [23:0] rgb_video_1_p7;

  Clock clock_1 (.out(clock_1_out));
  Counter #(.max('h3fff), .width(14)) counter_1 (
    .clk(clock_1_out), .Q(counter_1_q));  // open: clr, load, up, count, D, carry
  // RGB_Video rgb_video_1: pin names not known; wires that end beside it: counter_1_q, 1'b0, clock_1_out, 1'b1, counter_1_q[6:0], counter_1_q[13:7], rgb_video_1_p7
  ROM #(.addrWidth(14), .dataWidth(24)) rom_1 (.addr(counter_1_q), .data(rgb_video_1_p7));
endmodule
